# Fritzing sketch 19.2-turn-on-LED-if-someone-logged-in-remotely (saved by Fritzing 0.9.2b)
breadboards: 1

parts:
  Raspberry_Pi1 = Raspberry Pi 2
  LED1 = LED - 3mm [color="Red (633nm)" package="3 mm [THT]"]
  R1 = Resistor [tolerance=±5% resistance=470 package="0402 [SMD]"]

nets:
  N1: Raspberry_Pi1.GPIO21, LED1.anode
  N2: Raspberry_Pi1.GND, R1.Pin_0
  N3: LED1.cathode, R1.Pin_1

notes:
  GPIO 21
  LED (~ 1.8V)
