# Fritzing sketch 5.2 (saved by Fritzing 0.9.2b)
breadboards: 1

parts:
  Part1 = Arduino Uno (Rev3) - ICSP
  R1 = Resistor [tolerance=±5% resistance=100 package="0402 [SMD]"]
  R2 = Resistor [tolerance=±5% resistance=100 package="0402 [SMD]"]
  R3 = Resistor [tolerance=±5% resistance=100 package="0402 [SMD]"]
  LED1 = RGB LED (com. cathode, rbg) [package="5 mm [THT]"]
  S1 = Pushbutton [package=THT]

nets:
  N1: Part1.ICSP_MISO, Part1.D12/MISO, R1.Pin_0
  N2: Part1.ICSP_MOSI, Part1.D11_PWM/MOSI, R2.Pin_0
  N3: Part1.D10_PWM/SS, R3.Pin_0
  N4: Part1.D4, S1.leg1
  N5: Part1.5V, S1.leg0
  N6: Part1.GND, LED1.common_cathode
  N7: R1.Pin_1, LED1.red_anode
  N8: R2.Pin_1, LED1.green_anode
  N9: R3.Pin_1, LED1.blue_anode
