# Fritzing sketch 5.3 (saved by Fritzing 0.8.7b)

parts:
  Part1 = Arduino Uno (Rev3) - ICSP
  U1 = LCD-16X2 [package=lcd-16x2]
  U4 = POT [package=pot_mammoth]

nets:
  N1: Part1.ICSP_MISO, Part1.D12/MISO, U1.RS
  N2: Part1.ICSP_MOSI, Part1.D11_PWM/MOSI, U1.E
  GND: Part1.GND, U1.VSS, U1.R_W, U4.E
  N3: Part1.D2, U1.DB7
  N4: Part1.D3_PWM, U1.DB6
  N5: Part1.D4, U1.DB5
  N6: Part1.D5_PWM, U1.DB3, U1.DB4
  5V: Part1.5V, U1.VDD, U4.S
  N7: U1.VO, U4.A
