# Fritzing sketch 5.4 (saved by Fritzing 0.8.7b)

parts:
  Part1 = Arduino Uno (Rev3) - ICSP
  U1 = LCD-16X2 [package=lcd-16x2]
  U4 = POT [package=pot_mammoth]
  S1 = Pushbutton [package=THT]
  R1 = Resistor [tolerance=±5% resistance=100 package=THT]

nets:
  N1: Part1.ICSP_MISO, Part1.D12/MISO, U1.E
  N2: Part1.ICSP_MOSI, Part1.D11_PWM/MOSI, U1.DB3, U1.DB4
  N3: Part1.D8, U1.DB7
  N4: Part1.D9_PWM, U1.DB6
  N5: Part1.D10_PWM/SS, U1.DB5
  N6: Part1.D13/SCK, U1.RS
  GND: Part1.GND, U1.VSS, U1.R_W, U4.E, R1.Pin_1
  N7: Part1.D7, S1.leg1, R1.Pin_0
  5V: Part1.5V, U1.VDD, U4.S, S1.leg0
  N8: U1.VO, U4.A
