# Fritzing sketch 5.6 (saved by Fritzing 0.8.7b)

parts:
  Part1 = Arduino Uno (Rev3) - ICSP
  U1 = LCD-16X2 [package=lcd-16x2]
  U4 = POT [package=pot_mammoth]
  Matrix_keypad1 = KEYPAD 4x4
  R1 = Resistor [tolerance=±5% resistance=100 package=THT]
  LED1 = LED - 5mm [color="Red (633nm)" package="5 mm [THT]"]

nets:
  N1: Part1.A0, R1.Pin_1
  N2: Part1.ICSP_MISO, Part1.D12/MISO, U1.E
  N3: Part1.ICSP_MOSI, Part1.D11_PWM/MOSI, U1.DB3, U1.DB4
  GND: Part1.GND, U1.VSS, U1.R_W, U4.E, LED1.cathode
  N4: Part1.D8, U1.DB7
  N5: Part1.D9_PWM, U1.DB6
  N6: Part1.D10_PWM/SS, U1.DB5
  N7: Part1.D13/SCK, U1.RS
  N8: Part1.D0/RX, Matrix_keypad1.row4
  N9: Part1.D1/TX, Matrix_keypad1.row3
  N10: Part1.D2, Matrix_keypad1.row2
  N11: Part1.D3_PWM, Matrix_keypad1.row1
  N12: Part1.D4, Matrix_keypad1.col4
  N13: Part1.D5_PWM, Matrix_keypad1.col3
  N14: Part1.D6_PWM, Matrix_keypad1.col2
  N15: Part1.D7, Matrix_keypad1.col1
  5V: Part1.5V, U1.VDD, U4.S
  N16: U1.VO, U4.A

custom parts:
  KEYPAD 4x4: Matrix keypad 16 buttons, 4 rows x 4 columns
