# Fritzing sketch 7.2 (saved by Fritzing 0.8.7b)

parts:
  Part1 = Arduino Uno (Rev3) - ICSP
  U4 = POT [package=pot_mammoth]
  R1 = Resistor [tolerance=±5% resistance=100 package=THT]
  LED1 = LED - 5mm [color="Red (633nm)" package="5 mm [THT]"]

nets:
  N1: Part1.A0, U4.A
  N2: Part1.GND, U4.S, LED1.cathode
  N3: Part1.D3_PWM, R1.Pin_1
  N4: Part1.5V, U4.E
