# Fritzing sketch 7.3 (saved by Fritzing 0.8.7b)

parts:
  Part1 = Arduino Uno (Rev3) - ICSP
  R1 = Resistor [tolerance=±5% resistance=100 package=THT]
  LED1 = LED - 5mm [color="Red (633nm)" package="5 mm [THT]"]
  R2 = Photocell (LDR) [package=THT]
  R3 = Resistor [tolerance=±5% resistance=1k package=THT]

nets:
  N1: Part1.A0, R3.Pin_1
  N2: Part1.GND, LED1.cathode, R2.pin_0
  N3: Part1.D2, R1.Pin_1
  N4: Part1.5V, R3.Pin_0
