# Fritzing sketch 19.3-push-button-download-weather-from-inet (saved by Fritzing 0.9.2b)

parts:
  Raspberry_Pi1 = Raspberry Pi 2
  S1 = SWITCH-MOMENTARY-2 [package=tactile-switch-1101ne]

nets:
  N1: Raspberry_Pi1.GPIO21, S1.1
  N2: Raspberry_Pi1.GND, S1.2

notes:
  GPIO 21
  Momentary Switch
