# Fritzing sketch 20.1-lighting-the-tri-color-LED-based-on-CPU-load (saved by Fritzing 0.9.2b)
breadboards: 1

parts:
  Raspberry_Pi1 = Raspberry Pi 2
  RGB_LED = RGB LED (com. cathode, rgb) [package="5 mm [THT]"]
  part = Resistor [tolerance=±5% resistance=100 package="0805 [SMD]"]
  R2 = Resistor [tolerance=±5% resistance=100 package="0805 [SMD]"]
  R3 = Resistor [tolerance=±5% resistance=100 package="0805 [SMD]"]

nets:
  N1: Raspberry_Pi1.GND, RGB_LED.common_cathode
  N2: Raspberry_Pi1.GPIO21, R3.Pin_1
  N3: Raspberry_Pi1.GPIO20, R2.Pin_1
  N4: Raspberry_Pi1.GPIO16, part.Pin_1
  N5: RGB_LED.red_anode, part.Pin_0
  N6: RGB_LED.green_anode, R2.Pin_0
  N7: RGB_LED.blue_anode, R3.Pin_0

notes:
  RGB LED
  GPIO 21
