# Fritzing sketch 23.2-interfacing-a-temperature-sensor-and-recording-its-data-to-a-file (saved by Fritzing 0.9.2b)
breadboards: 1

parts:
  Raspberry_Pi1 = Raspberry Pi 2
  IC1 = IC, DIP package, 8 pins [chip_label=3002]
  T1 = LM35 Temperature Sensor [package="TO92 [THT]"]

nets:
  N1: Raspberry_Pi1.3v3, IC1.pin8
  N2: Raspberry_Pi1.GPIO10, IC1.pin5
  N3: Raspberry_Pi1.GPIO9, IC1.pin6
  N4: Raspberry_Pi1.GPIO11, IC1.pin7
  GND: Raspberry_Pi1.GND, IC1.pin4, T1.GND
  N5: Raspberry_Pi1.GPIO8, IC1.pin1
  N6: Raspberry_Pi1.5V, T1.+Vs
  N7: IC1.pin2, T1.Vout

notes:
  LM35 Temp Sensor
